# Fritzing sketch control-plate (saved by Fritzing 0.9.3b)
breadboards: 1

parts:
  S1 = Pushbutton [package="[THT]"]
  S2 = Pushbutton [package="[THT]"]
  S3 = Pushbutton [package="[THT]"]
  S4 = Pushbutton [package="[THT]"]
  S5 = Pushbutton [package="[THT]"]
  S6 = Pushbutton [package="[THT]"]
  LED1 = LED - 5mm [color="Red (633nm)" package="5 mm [THT]"]
  LED2 = LED - 5mm [color="Red (633nm)" package="5 mm [THT]"]
  LED3 = LED - 5mm [color="Red (633nm)" package="5 mm [THT]"]
  LED4 = LED - 5mm [color="Red (633nm)" package="5 mm [THT]"]
  LED5 = LED - 5mm [color="Red (633nm)" package="5 mm [THT]"]
  LED6 = LED - 5mm [color="Red (633nm)" package="5 mm [THT]"]
  LED7 = LED - 5mm [color="Red (633nm)" package="5 mm [THT]"]
  J1 = shrouded pin header, 10 pins [form="♂ (shrouded male)"]

nets:
  N1: S1.Pin_1, S2.Pin_3, S2.Pin_4, LED1.anode, LED2.anode, J1.pin3
  N2: S1.Pin_3, S1.Pin_4, S3.Pin_3, S3.Pin_4, S5.Pin_3, J1.pin7
  N3: S2.Pin_1, S2.Pin_2, S4.Pin_3, S4.Pin_4, S6.Pin_3, S6.Pin_4, J1.pin8
  N4: S3.Pin_2, S4.Pin_1, LED3.anode, LED6.anode, J1.pin2
  N5: S5.Pin_1, S5.Pin_2, S6.Pin_1, S6.Pin_2
  N6: LED1.cathode, LED3.cathode, LED5.cathode, J1.pin4
  N7: LED2.cathode, LED4.cathode, J1.pin5
  N8: LED4.anode, LED5.anode, LED7.anode, J1.pin1
  N9: LED6.cathode, LED7.cathode, J1.pin6
