# Fritzing sketch setup (saved by Fritzing 0.9.3b)
stripboards: 1
breadboards: 1

parts:
  J2 = longpad pin header, 8 pins [form="long pad"]
  KY-3 = Keyes Relay [package=THT]
  KY-4 = Keyes Relay [package=THT]
  KY-5 = Keyes Relay [package=THT]
  Part3 = Tessel 2
  LED1 = LED - 5mm [color="Blue (525nm)" package="5 mm [THT]"]
  LED2 = LED - 5mm [color="Blue (525nm)" package="5 mm [THT]"]
  LED3 = LED - 5mm [color="Red (633nm)" package="5 mm [THT]"]

nets:
  N1: J2.pin1, KY-4.C, KY-5.C, LED1.anode, LED2.anode, LED3.anode
  N2: J2.pin2, KY-3.C
  N3: J2.pin4, LED2.cathode
  N4: J2.pin5, LED1.cathode
  N5: J2.pin6, LED3.cathode
  N6: J2.pin7, KY-4.NO
  N7: J2.pin8, KY-3.NO, KY-5.NO
  N8: KY-3.signal, Part3.4
  N9: KY-3.power, KY-4.power, KY-5.power, Part3.5V
  N10: KY-3.ground, KY-4.ground, KY-5.ground, Part3.GND
  N11: KY-4.signal, Part3.5
  N12: KY-5.signal, Part3.6

notes:
  Latissima
  S4
  S5
  S6

custom parts:
  Keyes Relay: The Keyes 5V relay module is suitable for SCM development, home appliance control. It uses a 5V~12V TIL control signal which can control DC / AC signal.
  Tessel 2: Draft version of Tessel 2
